# Fritzing sketch imu_pcb (saved by Fritzing 1.0.6)
circuit board: 8.46667cm x 5.64444cm

parts:
  J2 = screw terminal, 10 pins
  J3 = female pin header, 10 pins [form="♀ (female)"]  # not connected
  J1 = female pin header, 10 pins [form="♀ (female)"]

nets:
  N1: J2.pin1, J1.pin1
  N2: J2.pin2, J1.pin2
  N3: J2.pin3, J1.pin3
  N4: J2.pin4, J1.pin4
  N5: J2.pin5, J1.pin5
  N6: J2.pin6, J1.pin6
  N7: J2.pin7, J1.pin7
  N8: J2.pin8, J1.pin8
  N9: J2.pin9, J1.pin9
  N10: J2.pin10, J1.pin10
